# Fritzing sketch esp-breakout-board (saved by Fritzing 0.9.9b)
perfboards: 2

parts:
  J1 = female pin header, 8 pins [form="♀ (female)"]  # not connected
  J2 = female pin header, 8 pins [form="♀ (female)"]  # not connected
  J3 = female pin header, 8 pins [form="♀ (female)"]  # not connected
  S1 = Pushbutton [package="[THT]"]
  S2 = Pushbutton [package="[THT]"]
  J4 = female pin header, 2 pins [form="♀ (female)"]  # not connected
  R1 = Resistor [tolerance=±5% resistance=10k package="0805 [SMD]"]  # not connected
  R2 = Resistor [tolerance=±5% resistance=10k package="0805 [SMD]"]  # not connected
  R3 = Resistor [tolerance=±5% resistance=10k package="0805 [SMD]"]  # not connected
  R4 = Resistor [tolerance=±5% resistance=10k package="0805 [SMD]"]  # not connected
  C4 = Electrolytic Capacitor [capacitance=0.47mF voltage=35V package="200 mil [THT, electrolytic]"]  # not connected
  U3 = V_REG_LD1117VXX [package=78xxl]  # not connected

nets:
  N1: S1.Pin_1, S1.Pin_2
  N2: S1.Pin_3, S1.Pin_4
  N3: S2.Pin_1, S2.Pin_2
  N4: S2.Pin_3, S2.Pin_4

notes:
  A0, 14, 12, 13, 4, 5, RX, TX
